// Logisim project Digital_Door_Access_System.circ as structural Verilog: 1 circuit, main circuit main
module main (
  input  in_1,
  input  in_2,
  input  in_3,
  input  in_4,
  output out_5
);

  wire not_1_out, xnor_1_out, xnor_2_out, xnor_3_out, xnor_4_out;

  xnor xnor_1 (xnor_1_out, in_1, 1'b1);
  xnor xnor_2 (xnor_2_out, in_2, 1'b0);
  xnor xnor_3 (xnor_3_out, in_3, 1'b1);
  xnor xnor_4 (xnor_4_out, in_4, 1'b1);
  and and_1 (out_5, xnor_1_out, xnor_2_out, xnor_3_out, xnor_4_out);
  not not_1 (not_1_out, out_5);
  LED led_1 (.in(out_5));
  LED led_2 (.in(not_1_out));
endmodule
