// Logisim project ddcaco2.circ as structural Verilog: 1 circuit, main circuit main
module main (
  input  H,
  input  S,
  input  M,
  input  W,
  output P,
  output A
);

  wire and_1_out, multiplexer_1_out, not_1_out, not_2_out;

  not not_1 (not_1_out, H);
  Multiplexer multiplexer_1 (.in0(not_1_out), .in1(S), .out(multiplexer_1_out), .sel(M));  // open: en
  not not_2 (not_2_out, W);
  or or_1 (A, not_2_out, H);
  and and_1 (and_1_out, multiplexer_1_out, not_1_out);
  and and_2 (P, and_1_out, W);
endmodule
